# Fritzing sketch sd_player (saved by Fritzing 0.9.10b)
breadboards: 1

parts:
  Part1 = Adafruit Feather M0 Express [part_number="Adafruit #3403"]
  Part2 = Mono 2.5W Class D Audio Amplifier - PAM8302
  Part3 = Adafruit MicroSD card breakout board [part_number="Adafruit #254"]
  R1 = Rotary Potentiometer (Small) [maximum_resistance=100kΩ knob_status=50% power=0.5W package=THT]
  R2 = Resistor [tolerance=±5% resistance=220 package="0603 [SMD]"]
  R3 = Resistor [tolerance=±5% resistance=220 package="0603 [SMD]"]
  R4 = Resistor [tolerance=±5% resistance=220 package="0603 [SMD]"]
  R5 = Resistor [tolerance=±5% resistance=220 package="0603 [SMD]"]
  R6 = Resistor [tolerance=±5% resistance=220 package="0603 [SMD]"]
  U1 = BUTTON-CONDUCTIVE [package=button-conductive]
  U2 = BUTTON-CONDUCTIVE [package=button-conductive]
  U3 = BUTTON-CONDUCTIVE [package=button-conductive]
  U4 = BUTTON-CONDUCTIVE [package=button-conductive]
  U5 = BUTTON-CONDUCTIVE [package=button-conductive]
  SP1 = SPEAKER [package=pcb_mount_speaker]

nets:
  GND: Part1.GND, Part2.GND, Part2.AIN-, Part3.GND, R1.leg1, U1.1, U2.1, U3.1, U4.1, U5.1
  N1: Part1.MISO, Part3.DO
  N2: Part1.MOSI, Part3.DI
  N3: Part1.SCK, Part3.CLK
  N4: Part1.A5, R6.Pin_0, U5.2
  N5: Part1.A4, R5.Pin_0, U4.2
  N6: Part1.A3, R4.Pin_0, U3.2
  N7: Part1.A2, R3.Pin_0, U2.2
  N8: Part1.A1, R2.Pin_0, U1.2
  N9: Part1.A0, R1.leg2
  +3V3: Part1.+3V3, Part3.+3V3, R2.Pin_1, R3.Pin_1, R4.Pin_1, R5.Pin_1, R6.Pin_1
  N10: Part1.VBUS, Part2.VCC
  N11: Part1.D5, Part3.CS
  N12: Part2.AIN+, R1.wiper
  N13: Part2.VO+, SP1.-
  N14: Part2.VO-, SP1.+

notes:
  Piezo mics used as analog buttons and shown as conductive sensors and purposely connected + (red wire) to GND

custom parts:
  Adafruit Feather M0 Express: We love all our Feathers equally, but this Feather is very special. It's our first Feather that is specifically designed for use with CircuitPython! CircuitPython is our beginner-oriented flavor of MicroPython - and as the name hints at, its a small but full-featured version of the popular Python programming language specifically for use with circuitry and electronics. That doesn't mean you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
  Mono 2.5W Class D Audio Amplifier - PAM8302: A super small but powerful mono amplifier able to deliver up to 2.5 Watts into 4-8 ohm impedance speakers. Inside the miniature chip is a class D controller, able to run from 2.0V-5.5VDC. Since the amp is a class D, its very efficient (over 90% efficient when driving an 8Ω speaker at over half a Watt) - making it perfect for portable and battery-powered projects.
  Adafruit MicroSD card breakout board: Not just a simple breakout board, this microSD adapter goes the extra mile - designed for ease of use. Onboard 5v->3v regulator provides 150mA for power-hungry cards 3v level shifting means you can use this with ease on either 3v or 5v systems Uses a proper level shifting chip, not resistors: less problems, and faster read/write access Use 3 or 4 digital pins to read and write 2Gb+ of storage!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
